// Digital circuit ALU8bits.dig as structural Verilog
module ALU8bits (
  input  [7:0] N,
  input  [2:0] S,
  input  CLK,
  output [7:0] MQ,
  output NEGACAO,
  output [7:0] AC,
  output OVER
);

  wire neg, Over_t, sMQ;
  wire [7:0] _000, _001, _010, _011, _100, _101, _110, _111, MQ0, MQ1, multiplexer_1_out, multiplexer_2_out;

  and and_1 (sMQ, S[0], S[1], ~S[2]);  // And
  Add #(.Bits(8)) SOMA (.a(AC), .b(N), .c_i(1'b0), .s(_000), .c_o(Over_t));
  Sub #(.Bits(8)) \SUBTRAÇÃO  (.a(AC), .b(N), .c_i(1'b0), .s(_001), .c_o(neg));
  Mul #(.Bits(8)) MULT (.a(AC), .b(N), .mul({MQ0, _010}));
  Div #(.Bits(8)) DIV (.a(AC), .b(N), .q(MQ1), .r(_011));
  LeftShift8bits Shift_esquerda (.A(AC), .S(_100));
  RightShift8bits u_S (.A(AC), .ARS(_101));
  nand8bits NAND (.A(AC), .B(N), .S(_110));
  XOR8bits XOR (.A(AC), .B(N), .S(_111));
  Multiplexer #(.Bits(8)) multiplexer_1 (.sel(sMQ), .in_0(MQ0), .in_1(MQ1), .out(multiplexer_1_out));
  Multiplexer #(.Selector_Bits(3), .Bits(8)) multiplexer_2 (
    .sel(S), .in_0(_000), .in_1(_001), .in_2(_010), .in_3(_011), .in_4(_100), .in_5(_101), .in_6(_110),
    .in_7(_111), .out(multiplexer_2_out));
  Register #(.Bits(8)) u_MQ (.D(multiplexer_1_out), .C(CLK), .en(1'b1), .Q(MQ));
  Register #(.Bits(8)) u_AC (.D(multiplexer_2_out), .C(CLK), .en(1'b1), .Q(AC));
  and and_2 (OVER, Over_t, ~S[0], ~S[1], ~S[2]);  // And
  and and_3 (NEGACAO, neg, S[0], ~S[1], ~S[2]);  // And

  // Other names for the same wires on the sheet: sAC[2:0] = S
endmodule
