// Digital circuit CU.dig as structural Verilog
module CU (
  input  clk,
  input  Botao,
  output PC,
  output MAR_OPCAO,
  output MAR_OPER,
  output IR
);

  wire S1, S3;

  Ring_counter ring_counter_1 (.Botao(Botao), .clk(clk), .S0(MAR_OPCAO), .S1(S1), .S2(MAR_OPER), .S3(S3), .S4(PC));
  xor xor_1 (IR, S1, S3);

  // Other names for the same wires on the sheet: S0 = MAR_OPCAO; S2 = MAR_OPER; S4 = PC
endmodule
