// Digital circuit Contador-4bits.dig as structural Verilog
module Contador_4bits (
  input  IN,
  input  CLR,
  output S3,
  output S2,
  output S1,
  output S0
);

  wire jk_ff_as_1_nq, jk_ff_as_2_nq, jk_ff_as_3_nq;

  JK_FF_AS jk_ff_as_1 (.Set(1'b0), .J(1'b1), .C(IN), .K(1'b1), .Clr(CLR), .Q(S0), .nQ(jk_ff_as_1_nq));
  JK_FF_AS jk_ff_as_2 (.Set(1'b0), .J(1'b1), .C(jk_ff_as_1_nq), .K(1'b1), .Clr(CLR), .Q(S1), .nQ(jk_ff_as_2_nq));
  JK_FF_AS jk_ff_as_3 (.Set(1'b0), .J(1'b1), .C(jk_ff_as_2_nq), .K(1'b1), .Clr(CLR), .Q(S2), .nQ(jk_ff_as_3_nq));
  JK_FF_AS jk_ff_as_4 (.Set(1'b0), .J(1'b1), .C(jk_ff_as_3_nq), .K(1'b1), .Clr(CLR), .Q(S3));  // open: nQ
endmodule
