// Digital circuit Ring-counter.dig as structural Verilog
module Ring_counter (
  input  Botao,
  input  clk,
  output S0,
  output S1,
  output S2,
  output S3,
  output S4
);

  D_FF_AS d_ff_as_1 (.Set(Botao), .D(S4), .C(clk), .Clr(1'b0), .Q(S0));  // open: nQ
  D_FF_AS d_ff_as_2 (.Set(1'b0), .D(S0), .C(clk), .Clr(1'b0), .Q(S1));  // open: nQ
  D_FF_AS d_ff_as_3 (.Set(1'b0), .D(S1), .C(clk), .Clr(1'b0), .Q(S2));  // open: nQ
  D_FF_AS d_ff_as_4 (.Set(1'b0), .D(S2), .C(clk), .Clr(1'b0), .Q(S3));  // open: nQ
  D_FF_AS d_ff_as_5 (.Set(1'b0), .D(S3), .C(clk), .Clr(1'b0), .Q(S4));  // open: nQ
endmodule
